# Fritzing sketch ESP32DevKitC-LoRa-1672 (saved by Fritzing 1.0.5)

parts:
  LoRa_Module2 = Ra-01 - LoRa Module SX1278 [part_number=SX1278]
  U1 = ESP32-38PinWide [part_number=ESP32-38PinWide]

nets:
  N1: LoRa_Module2.RST, U1.GPIO14
  N2: LoRa_Module2.NSS, U1.GPIO5
  N3: LoRa_Module2.SCK, U1.GPIO18
  N4: LoRa_Module2.(M)OSI, U1.GPIO23
  N5: LoRa_Module2.(M)ISO, U1.GPIO19
  GND: LoRa_Module2.GND, U1.GND
  N6: LoRa_Module2.3.3V, U1.3.3
  N7: LoRa_Module2.D0, U1.GPIO2
  N8: LoRa_Module2.D1, U1.GPIO4
  N9: LoRa_Module2.D2, U1.GPIO15

custom parts:
  Ra-01 - LoRa Module SX1278: The Ra-01 LoRa Module featuring the SX1278 engine by Semtech. Module by AI-Thinker. Module (Ra-01) specifications from: https://www.banggood.com/Ra-01-Smart-Electronics-SX1278-LoRa-Spread-Spectrum-Wireless-Module-Ultra-Far-10KM-433M-p-1130769.html Description: Power supply: DC1.8-3.7V(3.3V) Chip: SX1278 Frequency: 433Mhz Operating temperature: -40~+85°C On Sheild Description (may vary by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
  ESP32-38PinWide: Generic 38-Pin ESP32 with wide format (only access to one side of pins on a breadboard) based on Stephen Lilley's HiLetgo ESP-WROOM-32 ESP32 ESP-32S Development Board.
