# Fritzing sketch ESP32DevKitC-LoRa-1672 (saved by Fritzing 1.0.4)

parts:
  esp1 = ESP32 DevKitc V4
  LoRa_Module2 = Ra-01 - LoRa Module SX1278 [part_number=SX1278]

nets:
  N1: esp1.IO15, LoRa_Module2.D2
  N2: esp1.IO2, LoRa_Module2.D0
  N3: esp1.IO4, LoRa_Module2.D1
  N4: esp1.IO5, LoRa_Module2.NSS
  N5: esp1.IO18, LoRa_Module2.SCK
  N6: esp1.IO19, LoRa_Module2.(M)ISO
  N7: esp1.IO23, LoRa_Module2.(M)OSI
  GND: esp1.GND, LoRa_Module2.GND
  3V3: esp1.3V3, LoRa_Module2.3.3V
  N8: esp1.IO14, LoRa_Module2.RST

custom parts:
  ESP32 DevKitc V4: ESP32-DevKitC board with ESP32-WROOM-32 module. ESP32-DevKitC V4 is a small-sized ESP32-based development board produced by Espressif. Most of the pins on the ESP module are broken out to the pin headers on the board. The pins D0, D1, D2, D3, CMD and CLK are used internally for communication between ESP32 and SPI flash memory. They are grouped on both sides near the USB connector. Avoid using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
  Ra-01 - LoRa Module SX1278: The Ra-01 LoRa Module featuring the SX1278 engine by Semtech. Module by AI-Thinker. Module (Ra-01) specifications from: https://www.banggood.com/Ra-01-Smart-Electronics-SX1278-LoRa-Spread-Spectrum-Wireless-Module-Ultra-Far-10KM-433M-p-1130769.html Description: Power supply: DC1.8-3.7V(3.3V) Chip: SX1278 Frequency: 433Mhz Operating temperature: -40~+85°C On Sheild Description (may vary by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
